# Fritzing sketch arduino_schema (saved by Fritzing 0.9.3b)
breadboards: 1

parts:
  Componente1 = Arduino Nano (Rev3.0) (ICSP)
  Componente2 = Bluetooth HC-05 Macho
  S1 = Pushbutton [package="[THT]"]
  SW-1 = Vibration sensor module
  R1 = Resistor [tolerance=±5% resistance=220 package="2010 [SMD]"]

nets:
  GND: Componente1.GND, Componente2.GND, SW-1.Ground, R1.Pin_1
  N1: Componente1.D2, S1.Pin_1, S1.Pin_2, R1.Pin_0
  N2: Componente1.D6, SW-1.Digital_output
  N3: Componente1.D10, Componente2.TXD
  N4: Componente1.D11/MOSI, Componente2.RXD
  VCC: Componente1.5V, Componente2.VCC, S1.Pin_3, S1.Pin_4, SW-1.vcc

custom parts:
  Vibration sensor module: Single-roller type full induction trigger switch. When no vibration or tilt, the product is ON conduction state, and in the steady state, when a vibration or tilt, the switch will be rendered instantly disconnect the conductive resistance increases, generating a current pulse signal, thereby triggering circuit. The default state of the swith is close Digital output Supply voltage:3.3V-5V On-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
